# Fritzing sketch ADC-board (saved by Fritzing 0.7.12b)
breadboards: 1

parts:
  ADC = IC, DIP package, 20 pins [chip_label=ADC]
  I2C = female pin header, 2 pins [form="♀ (female)"]
  J1 = female pin header, 4 pins [form="♀ (female)"]
  J2 = female pin header, 4 pins [form="♀ (female)"]
  J3 = female pin header, 10 pins [form="♀ (female)"]
  J4 = female pin header, 3 pins [form="♀ (female)"]

nets:
  N1: ADC.pin1, J1.pin1, J1.pin2, J1.pin3, J1.pin4
  N2: ADC.pin4, J4.pin1
  N3: ADC.pin5, J4.pin2
  N4: ADC.pin6, J4.pin3
  N5: ADC.pin7, J3.pin8
  N6: ADC.pin8, J3.pin9
  N7: ADC.pin9, J3.pin10
  N8: ADC.pin11, I2C.pin2
  N9: ADC.pin12, J3.pin7
  N10: ADC.pin13, I2C.pin1
  N11: ADC.pin14, J3.pin6
  N12: ADC.pin15, J3.pin5
  N13: ADC.pin16, J3.pin4
  N14: ADC.pin17, J3.pin3
  N15: ADC.pin18, J3.pin2
  N16: ADC.pin19, J3.pin1
  N17: ADC.pin20, J2.pin1, J2.pin2, J2.pin3, J2.pin4

notes:
  AN8
  AN9
  AN7
  AN6
  AN2
  AN1
  AN0
  AN3
  AN4
  AN5
  sda
  scl
  pi.gbaman.info
  Address
  3v3
  gnd
  ADC Board
