# Fritzing sketch Button-board (saved by Fritzing 0.7.12b)
breadboards: 1

parts:
  S1 = Pushbutton [package="[THT]"]
  S2 = Pushbutton [package="[THT]"]
  GPIO = female pin header, 2 pins [form="♀ (female)"]
  GND = female pin header, 2 pins [form="♀ (female)"]
  3v3 = female pin header, 2 pins [form="♀ (female)"]
  R1 = Resistor [tolerance=±5% resistance=1k package="1206 [SMD]"]
  R4 = Resistor [tolerance=±5% resistance=1k package="1206 [SMD]"]
  R2 = Resistor [tolerance=±5% resistance=10k package="1206 [SMD]"]
  R3 = Resistor [tolerance=±5% resistance=10k package="1206 [SMD]"]

nets:
  N1: S1.Pin_1, S1.Pin_2, S2.Pin_1, S2.Pin_2, GND.pin1, GND.pin2, R1.Pin_1, R4.Pin_1
  N2: S1.Pin_3, S1.Pin_4, R2.Pin_1
  N3: S2.Pin_3, S2.Pin_4, R3.Pin_1
  N4: GPIO.pin1, R4.Pin_0
  N5: GPIO.pin2, R1.Pin_0
  N6: 3v3.pin1, 3v3.pin2, R2.Pin_0, R3.Pin_0

notes:
  GPIO
  GND
  Button
  3v3
  pi.gbaman.info
  S1
  S2
  1k
  10k
