# Fritzing sketch LED-Quad-board (saved by Fritzing 0.7.12b)
breadboards: 1

parts:
  LED3 = LED - 5mm [color="Red (633nm)" package="5 mm [THT]"]
  LED2 = LED - 5mm [color="Red (633nm)" package="5 mm [THT]"]
  3_4 = female pin header, 2 pins [form="♀ (female)"]
  gnd_3v3 = female pin header, 2 pins [form="♀ (female)"]
  R3 = Resistor [tolerance=±5% resistance=220 package="1206 [SMD]"]
  R1 = Resistor [tolerance=±5% resistance=220 package="1206 [SMD]"]
  R2 = Resistor [tolerance=±5% resistance=220 package="1206 [SMD]"]
  LED4 = LED - 5mm [color="Red (633nm)" package="5 mm [THT]"]
  R4 = Resistor [tolerance=±5% resistance=220 package="1206 [SMD]"]
  LED1 = LED - 5mm [color="Red (633nm)" package="5 mm [THT]"]
  1_2 = female pin header, 2 pins [form="♀ (female)"]
  LED5 = smd LED [color="Red (633nm)" package="1206 [SMD]"]
  R5 = Resistor [tolerance=±5% resistance=220 package="1206 [SMD]"]
  3v3 = female pin header, 2 pins [form="♀ (female)"]

nets:
  N1: LED3.cathode, R1.Pin_1
  N2: LED3.anode, 3_4.pin1
  N3: LED2.cathode, R3.Pin_1
  N4: LED2.anode, 1_2.pin2
  N5: 3_4.pin2, LED4.anode
  N6: gnd_3v3.pin1, gnd_3v3.pin2, R3.Pin_0, R1.Pin_0, R2.Pin_0, R4.Pin_0, R5.Pin_0
  N7: R2.Pin_1, LED4.cathode
  N8: R4.Pin_1, LED1.cathode
  N9: LED1.anode, 1_2.pin1
  N10: LED5.cathode, R5.Pin_1
  N11: LED5.anode, 3v3.pin1, 3v3.pin2

notes:
  pi.gbaman.info
  Quad-LED
  3v3
  GPIO
  GND
  220 ohm
  Status
