# Fritzing sketch Led-Duo-board (saved by Fritzing 0.7.12b)
breadboards: 1

parts:
  LED1 = LED - 5mm [color="Red (633nm)" package="5 mm [THT]"]
  LED2 = LED - 5mm [color="Red (633nm)" package="5 mm [THT]"]
  R2 = Resistor [tolerance=±5% resistance=220 package="1206 [SMD]"]
  R1 = Resistor [tolerance=±5% resistance=220 package="1206 [SMD]"]
  J1 = female pin header, 2 pins [form="♀ (female)"]
  J2 = female pin header, 2 pins [form="♀ (female)"]

nets:
  N1: LED1.cathode, R2.Pin_1
  N2: LED1.anode, J1.pin1
  N3: LED2.cathode, R1.Pin_1
  N4: LED2.anode, J1.pin2
  N5: R2.Pin_0, R1.Pin_0, J2.pin1, J2.pin2

notes:
  pi.gbaman.info
  GPIO
  220
  gnd
