# Fritzing sketch Ultrasonic-board (saved by Fritzing 0.7.12b)
breadboards: 1

parts:
  In = female pin header, 4 pins [form="♀ (female)"]
  5v = female pin header, 2 pins [form="♀ (female)"]
  GND = female pin header, 2 pins [form="♀ (female)"]
  GPIO = female pin header, 2 pins [form="♀ (female)"]
  R3 = Resistor [tolerance=±5% resistance=1k package="1206 [SMD]"]
  R1 = Resistor [tolerance=±5% resistance=2.2k package="1206 [SMD]"]
  R2 = Resistor [tolerance=±5% resistance=2.2k package="1206 [SMD]"]

nets:
  N1: In.pin1, 5v.pin1, 5v.pin2
  N2: In.pin2, R3.Pin_0
  N3: In.pin3, R1.Pin_0
  N4: In.pin4, GND.pin1, GND.pin2, R2.Pin_0
  N5: GPIO.pin1, GPIO.pin2, R3.Pin_1, R1.Pin_1, R2.Pin_1

notes:
  2.2k
  5v
  trig
  echo
  gnd
  GPIO
  pi.gbaman.info
  Ultrasonic
  1k
